# Fritzing sketch high_voltage_programmer (saved by Fritzing 0.9.3b)
stripboards: 1

parts:
  U1 = attiny85 [package=dip]
  Q1 = NPN-Transistor [part_number=2N2222A package="TO92 [THT]"]
  J1 = male pin header, 7 pins [form="♂ (male)"]
  R1 = Resistor [tolerance=±5% resistance=1k package=THT]
  R2 = Resistor [tolerance=±5% resistance=1k package=THT]
  R3 = Resistor [tolerance=±5% resistance=1k package=THT]
  R4 = Resistor [tolerance=±5% resistance=1k package=THT]
  R5 = Resistor [tolerance=±5% resistance=1k package=THT]
  J2 = female alternating pin header, 1 pin [form="♀ (female)"]
  R6 = Resistor [tolerance=±5% resistance=1k package=THT]

nets:
  N1: U1.Pin_1, Q1.C, R6.Pin_1
  N2: U1.Pin_2, R3.Pin_0
  GND: U1.Pin_4, Q1.E, J1.pin1
  N3: U1.Pin_5, R1.Pin_0
  N4: U1.Pin_6, R5.Pin_0
  N5: U1.Pin_7, R4.Pin_0
  N6: U1.Pin_8, J1.pin7
  N7: Q1.B, R2.Pin_0
  N8: J1.pin2, R2.Pin_1
  N9: J1.pin3, R3.Pin_1
  N10: J1.pin4, R4.Pin_1
  N11: J1.pin5, R5.Pin_1
  N12: J1.pin6, R1.Pin_1
  N13: J2.pin1, R6.Pin_0
