# Fritzing sketch regina_pong_composite_mod (saved by Fritzing 0.9.3b)
stripboards: 1

parts:
  C1 = Capacitor Polarized [package=cpol-radial-100uf-25v]
  Composite_out = male pin header, 1 pin [form="♂ (male)"]
  Ground_out = male pin header, 1 pin [form="♂ (male)"]
  R3 = Resistor [tolerance=±5% resistance=750 package=THT]
  Point2 = male pin header, 1 pin [form="♂ (male)"]
  Point3 = male pin header, 1 pin [form="♂ (male)"]
  Q1 = NPN-Transistor [package="TO92 [THT]"]
  IC1 = Voltage Regulator [package=78xxl]
  Point1 = male pin header, 1 pin [form="♂ (male)"]
  Point4 = male pin header, 1 pin [form="♂ (male)"]
  D1 = Rectifier Diode [package="Melf DO-213 AB [SMD]"]
  R2 = Resistor [tolerance=±5% resistance=75 package=THT]
  R1 = Resistor [tolerance=±5% resistance=75 package=THT]

nets:
  N1: C1.+, Q1.C, IC1.OUT
  N2: C1.-, Ground_out.pin1, IC1.GND, Point4.pin1, R2.Pin_0
  N3: Composite_out.pin1, D1.cathode, R1.Pin_1
  N4: R3.Pin_0, Q1.B
  N5: R3.Pin_1, Point2.pin1
  N6: Point3.pin1, D1.anode
  N7: Q1.E, R2.Pin_1, R1.Pin_0
  N8: IC1.IN, Point1.pin1
